// Logisim project Processor logisim.circ as structural Verilog: 8 circuits, main circuit Single Cycle Processor
module Single_Cycle_Processor (
  input  Reset,
  input  [3:0] Display_Address,
  output [31:0] out_3
);

  wire alu_1_eq, alu_1_gt, branch_unit_1_isbranchtacken, Clock, control_unit_1_isbeq, control_unit_1_isbgt,
       control_unit_1_isimmediate, control_unit_1_isret, control_unit_1_isst, control_unit_1_isubranch,
       control_unit_1_iswb, flags_flags_e, flags_flags_gt;
  wire [1:0] control_unit_1_isld;
  wire [3:0] multiplexer_3_out, multiplexer_6_out, multiplexer_7_out;
  wire [12:0] control_unit_1_alusignals;
  wire [26:0] rom_1_data;
  wire [31:0] adder_1_out, adder_2_out, adder_3_out, alu_1_aluresult, bit_extender_1_out,
       immediate_calculation_1_immx, memory_unit_1_idresult, multiplexer_1_out, multiplexer_2_out,
       multiplexer_4_out, multiplexer_5_out, PC_q, register_file_1_readd1, register_file_1_readd2,
       shifter_1_out;
  wire [31:27] rom_1_data_2;

  Register #(.width(32), .trigger("falling")) PC (
    .D(multiplexer_1_out), .Q(PC_q), .clk(Clock), .clr(Reset));  // open: en
  Multiplexer #(.width(32), .enable("false")) multiplexer_1 (
    .in0(adder_1_out), .in1(multiplexer_2_out), .out(multiplexer_1_out), .sel(branch_unit_1_isbranchtacken));
  assign bit_extender_1_out = {{5{rom_1_data[26]}}, rom_1_data};  // Bit_Extender bit_extender_1
  Adder #(.width(32)) adder_1 (.a(32'h4), .b(PC_q), .out(adder_1_out));  // open: cin, cout
  Shifter #(.width(32)) shifter_1 (.in(bit_extender_1_out), .\dist (5'b00010), .out(shifter_1_out));
  Clock u_Clock (.out(Clock));
  Immediate_calculation immediate_calculation_1 (.imm(rom_1_data[17:0]), .immx(immediate_calculation_1_immx));
  Adder #(.width(32)) adder_2 (.a(shifter_1_out), .b(PC_q), .out(adder_2_out));  // open: cin, cout
  Multiplexer #(.width(32), .enable("false")) multiplexer_2 (
    .in0(adder_2_out), .in1(register_file_1_readd1), .out(multiplexer_2_out), .sel(control_unit_1_isret));
  Adder #(.width(32)) adder_3 (.a(PC_q), .b(32'h4), .out(adder_3_out));  // open: cin, cout
  Hex_Digit_Display hex_digit_display_1 (.value(out_3[31:28]));  // open: dp
  ROM #(.addrWidth(24), .dataWidth(32)) rom_1 (.addr(PC_q[25:2]), .data({rom_1_data_2, rom_1_data}));  // open: sel
  Multiplexer #(.width(4), .enable("false")) multiplexer_3 (
    .in0(rom_1_data[17:14]), .in1(rom_1_data[25:22]), .out(multiplexer_3_out), .sel(control_unit_1_isst));
  register_file register_file_1 (
    .WriteD(multiplexer_5_out), .WriteE(control_unit_1_iswb), .ReadD1(register_file_1_readd1),
    .ReadD2(register_file_1_readd2), .DisplayD(out_3), .Clock(Clock), .Reset(Reset),
    .WriteA(multiplexer_7_out), .ReadA1(multiplexer_6_out), .ReadA2(multiplexer_3_out),
    .DisplayA(Display_Address));
  Multiplexer #(.width(32), .enable("false")) multiplexer_4 (
    .in0(register_file_1_readd2), .in1(immediate_calculation_1_immx), .out(multiplexer_4_out),
    .sel(control_unit_1_isimmediate));
  ALU alu_1 (
    .A(register_file_1_readd1), .B(multiplexer_4_out), .ALUsignals(control_unit_1_alusignals),
    .ALUresult(alu_1_aluresult), .gt(alu_1_gt), .eq(alu_1_eq));
  Memory_Unit memory_unit_1 (
    .MAR(alu_1_aluresult), .MDR(register_file_1_readd2), .IdResult(memory_unit_1_idresult),
    .isSt(control_unit_1_isst), .Clock(Clock), .isLd(control_unit_1_isld[0]), .Reset(Reset));
  Multiplexer #(.select(2), .width(32), .enable("false")) multiplexer_5 (
    .in0(alu_1_aluresult), .in1(memory_unit_1_idresult), .in2(adder_3_out), .out(multiplexer_5_out),
    .sel(control_unit_1_isld));  // open: in3
  Hex_Digit_Display hex_digit_display_2 (.value(out_3[23:20]));  // open: dp
  Hex_Digit_Display hex_digit_display_3 (.value(out_3[27:24]));  // open: dp
  Multiplexer #(.width(4), .enable("false")) multiplexer_6 (
    .in0(rom_1_data[21:18]), .in1(4'b1111), .out(multiplexer_6_out), .sel(control_unit_1_isret));
  flags flags (
    .isCMP(control_unit_1_alusignals[0]), .gt(alu_1_gt), .eq(alu_1_eq), .flags_GT(flags_flags_gt),
    .flags_E(flags_flags_e));
  Hex_Digit_Display hex_digit_display_4 (.value(out_3[19:16]));  // open: dp
  Control_Unit control_unit_1 (
    .I_bit(rom_1_data[26]), .opcode(rom_1_data_2), .isSt(control_unit_1_isst), .isLd(control_unit_1_isld[0]),
    .isBeq(control_unit_1_isbeq), .isBgt(control_unit_1_isbgt), .isRet(control_unit_1_isret),
    .isImmediate(control_unit_1_isimmediate), .isWb(control_unit_1_iswb),
    .isUbranch(control_unit_1_isubranch), .isCall(control_unit_1_isld[1]),
    .ALUsignals(control_unit_1_alusignals));
  Branch_Unit branch_unit_1 (
    .isBeq(control_unit_1_isbeq), .flags_E(flags_flags_e), .isUBranch(control_unit_1_isubranch),
    .isBgt(control_unit_1_isbgt), .flags_GT(flags_flags_gt), .isBranchTacken(branch_unit_1_isbranchtacken));
  Hex_Digit_Display hex_digit_display_5 (.value(out_3[15:12]));  // open: dp
  Hex_Digit_Display hex_digit_display_6 (.value(out_3[11:8]));  // open: dp
  Hex_Digit_Display hex_digit_display_7 (.value(out_3[7:4]));  // open: dp
  Multiplexer #(.width(4), .enable("false")) multiplexer_7 (
    .in0(rom_1_data[25:22]), .in1(4'b1111), .out(multiplexer_7_out), .sel(control_unit_1_isld[1]));
  Hex_Digit_Display hex_digit_display_8 (.value(out_3[3:0]));  // open: dp

  // Notes on the sheet:
  //   isBranchTaken
  //   branchTarget
  //   isBranchTaken
  //   branchTarget
  //   pc+4
  //   imm. calculation
  //   offset
  //   pc
  //   Instruction memory
  //   immx
  //   pc
  //   SINGLE CYCLE PROCESSOR
  //   instruction
  //   contents of rom_1 (hex, n*v repeats v):
  //   4880003 4c80003 98000002 2c000001 88000003 4c400001 a0000000 fb80008 7c380000 7ff80004 c000001
  //   9ffffff8 77f80004 74380000 7b80008 10404000 a0000000
  //   rs2
  //   rd
  //   op2
  //   op1
  //   isImmediate
  //   is>
  //   ALU
  //   is=
  //   aluResult
  //   Memory Unit
  //   data
  //   opcode
  //   I bit
  //   rs1
  //   isRet
  //   isSt
  //   A
  //   E
  //   Register File
  //   D
  //   isRet
  //   ALUsignals
  //   flags(GT)
  //   flags(E)
  //   isCmp
  //   isSt
  //   isLd
  //   ldResult
  //   isLd
  //   isCall
  //   Display Register
  //   isSt
  //   isLd
  //   isBeq
  //   isBgt
  //   isRet
  //   Control
  //   Unit
  //   isImmediate
  //   isWb
  //   isUBranch
  //   isCall
  //   ALUSignals
  //   address
  //   isWb
  //   data
  //   isBeq
  //   BU
  //   isBgt
  //   isUBranch
endmodule

module ALU (
  input  [31:0] A,
  input  [31:0] B,
  input  [12:0] ALUsignals,
  output [31:0] ALUresult,
  output gt,
  output eq
);

  wire [31:0] adder_1_out, and_1_out, divider_1_out, divider_1_rem, multiplier_1_out, not_1_out, or_1_out,
       shifter_1_out, shifter_2_out, shifter_3_out, subtractor_1_out;

  Adder #(.width(32)) adder_1 (.a(A), .b(B), .out(adder_1_out));  // open: cin, cout
  Subtractor #(.width(32)) subtractor_1 (.a(A), .b(B), .out(subtractor_1_out));  // open: bin, bout
  Multiplier #(.width(32)) multiplier_1 (.a(A), .b(B), .out(multiplier_1_out));  // open: cin, cout
  Divider #(.width(32)) divider_1 (.a(A), .b(B), .out(divider_1_out), .rem(divider_1_rem));  // open: upper
  Comparator #(.width(32)) comparator_1 (.a(A), .b(B), .gt(gt), .eq(eq));  // open: lt
  Shifter #(.width(32)) shifter_1 (.in(A), .\dist (B[4:0]), .out(shifter_1_out));
  Shifter #(.width(32), .shift("lr")) shifter_2 (.in(A), .\dist (B[4:0]), .out(shifter_2_out));
  Shifter #(.width(32), .shift("ar")) shifter_3 (.in(A), .\dist (B[4:0]), .out(shifter_3_out));
  assign not_1_out = ~A;  // NOT_Gate not_1, 32 bits wide
  assign and_1_out = A & B;  // AND_Gate and_1, 32 bits wide
  assign or_1_out = A | B;  // OR_Gate or_1, 32 bits wide
  assign ALUresult = ALUsignals[1] ? adder_1_out : 32'bz;  // Controlled_Buffer controlled_buffer_1
  assign ALUresult = ALUsignals[2] ? subtractor_1_out : 32'bz;  // Controlled_Buffer controlled_buffer_2
  assign ALUresult = ALUsignals[3] ? multiplier_1_out : 32'bz;  // Controlled_Buffer controlled_buffer_3
  assign ALUresult = ALUsignals[4] ? divider_1_out : 32'bz;  // Controlled_Buffer controlled_buffer_4
  assign ALUresult = ALUsignals[5] ? divider_1_rem : 32'bz;  // Controlled_Buffer controlled_buffer_5
  assign ALUresult = ALUsignals[6] ? B : 32'bz;  // Controlled_Buffer controlled_buffer_6
  assign ALUresult = ALUsignals[7] ? shifter_1_out : 32'bz;  // Controlled_Buffer controlled_buffer_7
  assign ALUresult = ALUsignals[8] ? shifter_2_out : 32'bz;  // Controlled_Buffer controlled_buffer_8
  assign ALUresult = ALUsignals[9] ? shifter_3_out : 32'bz;  // Controlled_Buffer controlled_buffer_9
  assign ALUresult = ALUsignals[10] ? not_1_out : 32'bz;  // Controlled_Buffer controlled_buffer_10
  assign ALUresult = ALUsignals[11] ? and_1_out : 32'bz;  // Controlled_Buffer controlled_buffer_11
  assign ALUresult = ALUsignals[12] ? or_1_out : 32'bz;  // Controlled_Buffer controlled_buffer_12

  // Notes on the sheet:
  //   cmp
  //   adder
  //   sub
  //   mul
  //   div
  //   lsl
  //   lsr
  //   asr
endmodule

module flags (
  input  isCMP,
  input  gt,
  input  eq,
  output flags_GT,
  output flags_E
);

  D_Flip_Flop d_ff_1 (.clk(isCMP), .D(gt), .Q(flags_GT));  // open: Qn, preset, en, reset
  D_Flip_Flop d_ff_2 (.clk(isCMP), .D(eq), .Q(flags_E));  // open: Qn, preset, en, reset
endmodule

module Immediate_calculation (
  input  [17:0] imm,
  output [31:0] immx
);

  wire [31:0] bit_extender_1_out, bit_extender_2_out, shifter_1_out;

  assign bit_extender_1_out = {{16{imm[15]}}, imm[15:0]};  // Bit_Extender bit_extender_1
  assign bit_extender_2_out = {{16{1'b0}}, imm[15:0]};  // Bit_Extender bit_extender_2
  Shifter #(.width(32)) shifter_1 (.in(bit_extender_2_out), .\dist (5'b10000), .out(shifter_1_out));
  Multiplexer #(.select(2), .width(32), .enable("false")) multiplexer_1 (
    .in0(bit_extender_1_out), .in1(bit_extender_2_out), .in2(shifter_1_out), .out(immx), .sel(imm[17:16]));  // open: in3

  // Notes on the sheet:
  //   signed
  //   unsigned
  //   high
endmodule

module Memory_Unit (
  input  [31:0] MAR,
  input  [31:0] MDR,
  input  isSt,
  input  Clock,
  input  isLd,
  input  Reset,
  output [31:0] IdResult
);

  RAM #(.addrWidth(24), .dataWidth(32), .bus("separate")) ram_1 (
    .addr(MAR[25:2]), .din(MDR), .data(IdResult), .str(isSt), .clk(Clock), .ld(isLd), .clr(Reset));  // open: sel
endmodule

module Branch_Unit (
  input  isBeq,
  input  flags_E,
  input  isUBranch,
  input  isBgt,
  input  flags_GT,
  output isBranchTacken
);

  wire and_1_out, and_2_out;

  and and_1 (and_1_out, isBeq, flags_E);
  and and_2 (and_2_out, isBgt, flags_GT);
  or or_1 (isBranchTacken, and_1_out, isUBranch, and_2_out);
endmodule

module Control_Unit (
  input  I_bit,
  input  [4:0] opcode,
  output isSt,
  output isLd,
  output isBeq,
  output isBgt,
  output isRet,
  output isImmediate,
  output isWb,
  output isUbranch,
  output isCall,
  output [12:0] ALUsignals
);

  wire and_6_out, and_7_out, and_8_out, and_9_out, and_10_out, and_12_out, and_13_out, nand_1_out;

  nand nand_1 (nand_1_out, opcode[0], opcode[1]);
  and and_1 (isSt, opcode[0], opcode[1], opcode[2], opcode[3], ~opcode[4]);  // AND_Gate
  and and_2 (isLd, ~opcode[0], opcode[1], opcode[2], opcode[3], ~opcode[4]);  // AND_Gate
  and and_3 (isBeq, ~opcode[0], ~opcode[1], ~opcode[2], ~opcode[3], opcode[4]);  // AND_Gate
  and and_4 (isBgt, opcode[0], ~opcode[1], ~opcode[2], ~opcode[3], opcode[4]);  // AND_Gate
  and and_5 (isRet, ~opcode[0], ~opcode[1], opcode[2], ~opcode[3], opcode[4]);  // AND_Gate
  and and_6 (and_6_out, opcode[0], ~opcode[1], opcode[2], ~opcode[4]);  // AND_Gate
  and and_7 (and_7_out, opcode[0], opcode[2], opcode[3], ~opcode[4]);  // AND_Gate
  and and_8 (and_8_out, opcode[4], nand_1_out);
  and and_9 (and_9_out, opcode[1], ~opcode[2], ~opcode[3], opcode[4]);  // AND_Gate
  and and_10 (and_10_out, ~opcode[0], ~opcode[1], opcode[2], ~opcode[3], opcode[4]);  // AND_Gate
  and and_11 (isCall, opcode[0], opcode[1], ~opcode[2], ~opcode[3], opcode[4]);  // AND_Gate
  and and_12 (and_12_out, ~opcode[0], ~opcode[1], ~opcode[2], ~opcode[3], ~opcode[4]);  // AND_Gate
  and and_13 (and_13_out, opcode[1], opcode[2], opcode[3], ~opcode[4]);  // AND_Gate
  and isSub (ALUsignals[2], opcode[0], ~opcode[1], ~opcode[2], ~opcode[3], ~opcode[4]);  // AND_Gate
  and isCmp (ALUsignals[0], opcode[0], ~opcode[1], opcode[2], ~opcode[3], ~opcode[4]);  // AND_Gate
  and isMul (ALUsignals[3], ~opcode[0], opcode[1], ~opcode[2], ~opcode[3], ~opcode[4]);  // AND_Gate
  and isDiv (ALUsignals[4], opcode[0], opcode[1], ~opcode[2], ~opcode[3], ~opcode[4]);  // AND_Gate
  and isMod (ALUsignals[5], ~opcode[0], ~opcode[1], opcode[2], ~opcode[3], ~opcode[4]);  // AND_Gate
  and isLsl (ALUsignals[7], ~opcode[0], opcode[1], ~opcode[2], opcode[3], ~opcode[4]);  // AND_Gate
  and isLsr (ALUsignals[8], opcode[0], opcode[1], ~opcode[2], opcode[3], ~opcode[4]);  // AND_Gate
  and isAsr (ALUsignals[9], ~opcode[0], ~opcode[1], opcode[2], opcode[3], ~opcode[4]);  // AND_Gate
  and isOr (ALUsignals[12], opcode[0], opcode[1], opcode[2], ~opcode[3], ~opcode[4]);  // AND_Gate
  and isAnd (ALUsignals[11], ~opcode[0], opcode[1], opcode[2], ~opcode[3], ~opcode[4]);  // AND_Gate
  and isNot (ALUsignals[10], ~opcode[0], ~opcode[1], ~opcode[2], opcode[3], ~opcode[4]);  // AND_Gate
  and isMov (ALUsignals[6], opcode[0], ~opcode[1], ~opcode[2], opcode[3], ~opcode[4]);  // AND_Gate
  or or_1 (isUbranch, and_9_out, and_10_out);
  or isAdd (ALUsignals[1], and_12_out, and_13_out);
  nor nor_1 (isWb, and_6_out, and_7_out, and_8_out);

  assign isImmediate = I_bit;

  // Notes on the sheet:
  //   op1
  //   op2
  //   op3
  //   op4
  //   op5
endmodule

module register_file (
  input  Clock,
  input  Reset,
  input  [31:0] WriteD,
  input  [3:0] ReadA1,
  input  WriteE,
  input  [3:0] WriteA,
  input  [3:0] ReadA2,
  input  [3:0] DisplayA,
  output [31:0] ReadD1,
  output [31:0] ReadD2,
  output [31:0] DisplayD
);

  wire demultiplexer_1_out0, demultiplexer_1_out1, demultiplexer_1_out2, demultiplexer_1_out3,
       demultiplexer_1_out4, demultiplexer_1_out5, demultiplexer_1_out6, demultiplexer_1_out7,
       demultiplexer_1_out8, demultiplexer_1_out9, demultiplexer_1_out10, demultiplexer_1_out11,
       demultiplexer_1_out12, demultiplexer_1_out13, demultiplexer_1_out14, demultiplexer_1_out15,
       multiplexer_2_out, or_1_out, or_2_out;
  wire [31:0] multiplexer_1_out, r0_q, r1_q, r2_q, r3_q, r4_q, r5_q, r6_q, r7_q, r8_q, r9_q, r10_q, r11_q,
       r12_q, r13_q, r14_q, r15_q;

  Demultiplexer #(.select(4), .disabled(0), .enable("false")) demultiplexer_1 (
    .out0(demultiplexer_1_out0), .out1(demultiplexer_1_out1), .out2(demultiplexer_1_out2),
    .out3(demultiplexer_1_out3), .out4(demultiplexer_1_out4), .out5(demultiplexer_1_out5),
    .out6(demultiplexer_1_out6), .out7(demultiplexer_1_out7), .out8(demultiplexer_1_out8),
    .out9(demultiplexer_1_out9), .out10(demultiplexer_1_out10), .out11(demultiplexer_1_out11),
    .out12(demultiplexer_1_out12), .out13(demultiplexer_1_out13), .out14(demultiplexer_1_out14),
    .out15(demultiplexer_1_out15), .in(WriteE), .sel(WriteA));
  Multiplexer #(.width(32), .enable("false")) multiplexer_1 (
    .in0(WriteD), .in1(32'h3fffffc), .out(multiplexer_1_out), .sel(Reset));
  or or_1 (or_1_out, demultiplexer_1_out14, Reset);
  or or_2 (or_2_out, Clock, Reset);
  Multiplexer #(.enable("false")) multiplexer_2 (.in0(or_2_out), .out(multiplexer_2_out), .sel(1'b0));  // open: in1
  Register #(.width(32)) r0 (.D(WriteD), .en(demultiplexer_1_out0), .Q(r0_q), .clk(Clock), .clr(Reset));
  Register #(.width(32)) r1 (.D(WriteD), .en(demultiplexer_1_out1), .Q(r1_q), .clk(Clock), .clr(Reset));
  Register #(.width(32)) r2 (.D(WriteD), .en(demultiplexer_1_out2), .Q(r2_q), .clk(Clock), .clr(Reset));
  Register #(.width(32)) r3 (.D(WriteD), .en(demultiplexer_1_out3), .Q(r3_q), .clk(Clock), .clr(Reset));
  Register #(.width(32)) r4 (.D(WriteD), .en(demultiplexer_1_out4), .Q(r4_q), .clk(Clock), .clr(Reset));
  Register #(.width(32)) r5 (.D(WriteD), .en(demultiplexer_1_out5), .Q(r5_q), .clk(Clock), .clr(Reset));
  Register #(.width(32)) r6 (.D(WriteD), .en(demultiplexer_1_out6), .Q(r6_q), .clk(Clock), .clr(Reset));
  Register #(.width(32)) r7 (.D(WriteD), .en(demultiplexer_1_out7), .Q(r7_q), .clk(Clock), .clr(Reset));
  Register #(.width(32)) r8 (.D(WriteD), .en(demultiplexer_1_out8), .Q(r8_q), .clk(Clock), .clr(Reset));
  Register #(.width(32)) r9 (.D(WriteD), .en(demultiplexer_1_out9), .Q(r9_q), .clk(Clock), .clr(Reset));
  Register #(.width(32)) r10 (.D(WriteD), .en(demultiplexer_1_out10), .Q(r10_q), .clk(Clock), .clr(Reset));
  Register #(.width(32)) r11 (.D(WriteD), .en(demultiplexer_1_out11), .Q(r11_q), .clk(Clock), .clr(Reset));
  Register #(.width(32)) r12 (.D(WriteD), .en(demultiplexer_1_out12), .Q(r12_q), .clk(Clock), .clr(Reset));
  Register #(.width(32)) r13 (.D(WriteD), .en(demultiplexer_1_out13), .Q(r13_q), .clk(Clock), .clr(Reset));
  Register #(.width(32)) r14 (.D(multiplexer_1_out), .en(or_1_out), .Q(r14_q), .clk(multiplexer_2_out));  // open: clr
  Register #(.width(32)) r15 (.D(WriteD), .en(demultiplexer_1_out15), .Q(r15_q), .clk(Clock), .clr(Reset));
  Multiplexer #(.select(4), .width(32), .disabled(0), .enable("false")) multiplexer_3 (
    .in0(r0_q), .in1(r1_q), .in2(r2_q), .in3(r3_q), .in4(r4_q), .in5(r5_q), .in6(r6_q), .in7(r7_q),
    .in8(r8_q), .in9(r9_q), .in10(r10_q), .in11(r11_q), .in12(r12_q), .in13(r13_q), .in14(r14_q),
    .in15(r15_q), .out(ReadD1), .sel(ReadA1));
  Multiplexer #(.select(4), .width(32), .disabled(0), .enable("false")) multiplexer_4 (
    .in0(r0_q), .in1(r1_q), .in2(r2_q), .in3(r3_q), .in4(r4_q), .in5(r5_q), .in6(r6_q), .in7(r7_q),
    .in8(r8_q), .in9(r9_q), .in10(r10_q), .in11(r11_q), .in12(r12_q), .in13(r13_q), .in14(r14_q),
    .in15(r15_q), .out(ReadD2), .sel(ReadA2));
  Multiplexer #(.select(4), .width(32), .disabled(0), .enable("false")) multiplexer_5 (
    .in0(r0_q), .in1(r1_q), .in2(r2_q), .in3(r3_q), .in4(r4_q), .in5(r5_q), .in6(r6_q), .in7(r7_q),
    .in8(r8_q), .in9(r9_q), .in10(r10_q), .in11(r11_q), .in12(r12_q), .in13(r13_q), .in14(r14_q),
    .in15(r15_q), .out(DisplayD), .sel(DisplayA));
endmodule
